// Digital circuit CPU.dig as structural Verilog
module CPU (
  input  clk
);

  wire A_LD_CDATA, A_OUT_CDATA, and_1_out, and_2_out, and_3_out, CDATA_TO_CADDRH, CDATA_TO_CADDRL,
       IR_LD_XDATA, MARH_LD_CADDRH, MARL_LD_CADDRL, MBR_LD_CDATA, MBR_LD_XDATA, MBR_OUT_CDATA, MBR_OUT_XDATA,
       MEM_LD_XDATA, MEM_OUT_XDATA, not_1_out, or_1_out, or_2_out, PC_INC, PC_OUT_CADDR, STASH_LD_CDATA,
       STASH_OUT_CDATA;
  wire [7:0] A, driver_1_out, driver_5_out, IR, MARH, MARL, MBR, multiplexer_1_out, ROM_d, STASH;
  wire [15:0] add_1_s, PC;
  wire [15:8] driver_1_out_2;

  Register #(.Bits(16)) u_PC (.D(add_1_s), .C(clk), .en(PC_INC), .Q(PC));
  assign {driver_1_out_2, driver_1_out} = PC_OUT_CADDR ? PC : 16'bz;  // Driver driver_1
  Add #(.Bits(16)) add_1 (.a(PC), .b(16'h1), .c_i(1'b0), .s(add_1_s));  // open: c_o
  Register #(.Bits(8)) MAR_H (.D(driver_1_out_2), .C(clk), .en(MARH_LD_CADDRH), .Q(MARH));
  Register #(.Bits(8)) MAR_L (.D(driver_1_out), .C(clk), .en(MARL_LD_CADDRL), .Q(MARL));
  assign driver_1_out = CDATA_TO_CADDRL ? driver_5_out : 8'bz;  // Driver driver_2
  and and_1 (and_1_out, MARH[7], MEM_OUT_XDATA);
  assign driver_1_out_2 = CDATA_TO_CADDRH ? driver_5_out : 8'bz;  // Driver driver_3
  ROM #(.AddrBits(14), .Bits(8)) ROM (.A({MARH[5:0], MARL}), .sel(and_1_out), .D(ROM_d));
  or or_1 (or_1_out, MEM_LD_XDATA, MEM_OUT_XDATA);
  not not_1 (not_1_out, MARH[7]);
  Multiplexer #(.Bits(8)) multiplexer_1 (
    .sel(MBR_LD_CDATA), .in_0(ROM_d), .in_1(driver_5_out), .out(multiplexer_1_out));
  Seven_Seg_Hex seven_seg_hex_1 (.d(MARH[3:0]), .dp(1'b0));
  Seven_Seg_Hex seven_seg_hex_2 (.d(MARH[7:4]), .dp(1'b0));
  Register #(.Bits(8)) u_MBR (.D(multiplexer_1_out), .C(clk), .en(or_2_out), .Q(MBR));
  or or_2 (or_2_out, MBR_LD_CDATA, MBR_LD_XDATA);
  Seven_Seg_Hex seven_seg_hex_3 (.d(MARL[3:0]), .dp(1'b0));
  Seven_Seg_Hex seven_seg_hex_4 (.d(MARL[7:4]), .dp(1'b0));
  and and_2 (and_2_out, or_1_out, not_1_out);
  and and_3 (and_3_out, MEM_LD_XDATA, clk);
  Seven_Seg_Hex seven_seg_hex_5 (.d(MBR[7:4]), .dp(1'b0));
  assign ROM_d = MBR_OUT_XDATA ? MBR : 8'bz;  // Driver driver_4
  assign driver_5_out = MBR_OUT_CDATA ? MBR : 8'bz;  // Driver driver_5
  Seven_Seg_Hex seven_seg_hex_6 (.d(PC[15:12]), .dp(1'b0));
  Seven_Seg_Hex seven_seg_hex_7 (.d(MBR[3:0]), .dp(1'b0));
  Seven_Seg_Hex seven_seg_hex_8 (.d(PC[7:4]), .dp(1'b0));
  Seven_Seg_Hex seven_seg_hex_9 (.d(PC[11:8]), .dp(1'b0));
  Seven_Seg_Hex seven_seg_hex_10 (.d(PC[3:0]), .dp(1'b0));
  RAMSinglePortSel #(.AddrBits(14), .isProgramMemory("true"), .Bits(8)) RAM (
    .A({MARH[5:0], MARL}), .CS(and_2_out), .WE(and_3_out), .OE(MEM_OUT_XDATA), .D(ROM_d));
  Seven_Seg_Hex seven_seg_hex_11 (.d(IR[3:0]), .dp(1'b0));
  Seven_Seg_Hex seven_seg_hex_12 (.d(IR[7:4]), .dp(1'b0));
  Seven_Seg_Hex seven_seg_hex_13 (.d(A[3:0]), .dp(1'b0));
  Seven_Seg_Hex seven_seg_hex_14 (.d(A[7:4]), .dp(1'b0));
  Register #(.Bits(8)) u_IR (.D(ROM_d), .C(clk), .en(IR_LD_XDATA), .Q(IR));
  Seven_Seg_Hex seven_seg_hex_15 (.d(STASH[7:4]), .dp(1'b0));
  Seven_Seg_Hex seven_seg_hex_16 (.d(STASH[3:0]), .dp(1'b0));
  Register #(.Bits(8)) u_A (.D(driver_5_out), .C(clk), .en(A_LD_CDATA), .Q(A));
  Control_Unit control_unit_1 (
    .Nin(1'b0), .Vin(1'b0), .Zin(1'b0), .Cin(1'b0), .IRin(IR), .ClockIn(clk), .HALT(PC_OUT_CADDR),
    .MEM_LD_XDATA(MARH_LD_CADDRH), .MEM_OUT_XDATA(IR_LD_XDATA), .IR_LD_XDATA(PC_INC),
    .MBR_LD_XDATA(MBR_LD_XDATA), .MBR_OUT_XDATA(MBR_OUT_CDATA), .MBR_LD_CDATA(A_LD_CDATA),
    .MBR_OUT_CDATA(MEM_OUT_XDATA), .MARL_LD_CADDRL(MEM_LD_XDATA), .MARH_LD_CADDRH(MBR_OUT_XDATA),
    .CDATA_TO_ADDRL(MBR_LD_CDATA), .CDATA_TO_ADDRH(A_OUT_CDATA), .PC_INC(MARL_LD_CADDRL),
    .PC_LD_ADD(CDATA_TO_CADDRH), .PC_OUT_CADDR(CDATA_TO_CADDRL), .PCL_LD_CADDRL(STASH_LD_CDATA),
    .PCH_LD_CADDRH(STASH_OUT_CDATA));  // open: RESET, STASH_LD_CDATA, STASH_OUT_CDATA, A_LD_CDATA, A_OUT_CDATA, X_LDCDATA, X_OUT_CDATA, Y_LD_CDATA, Y_OUT_CDATA, PN_LD, V_LD, Z_LD, PC_LD, P_SRC_0, P_SRC_1, ALUA_LD_DATA, ALU_B_LD_CDATA, ALUP_LD_P, ALUR_OUT_CDATA, ALU_OP0, ALU_OP_1, ALU_OP_2
  assign driver_5_out = A_OUT_CDATA ? A : 8'bz;  // Driver driver_6
  Register #(.Bits(8)) u_STASH (.D(driver_5_out), .C(clk), .en(STASH_LD_CDATA), .Q(STASH));
  assign driver_5_out = STASH_OUT_CDATA ? STASH : 8'bz;  // Driver driver_7

  // Other names for the same wires on the sheet: P0_Clock = clk

  // Notes on the sheet:
  //   CADDRL Bus
  //   XADDR
  //   High bit 
  //     set => ROM
  //     unset => RAM
  //   CADDRH Bus
  //   contents of ROM (hex, n*v repeats v):
  //   a9,42
  //   CDATA Bus
  //   XDATA Bus
  //   MAR
  //   MBR
  //   PC
  //   IR
  //   A
  //   STASH
endmodule
